# Fritzing sketch 3-4 (saved by Fritzing 0.9.4)
breadboards: 1

parts:
  LED1 = LED - 5mm [color="Red (633nm)" package="5 mm [THT]"]
  LED2 = LED - 5mm [color="Red (633nm)" package="5 mm [THT]"]
  LED3 = LED - 5mm [color="Red (633nm)" package="5 mm [THT]"]
  LED4 = LED - 5mm [color="Red (633nm)" package="5 mm [THT]"]
  LED5 = LED - 5mm [color="Red (633nm)" package="5 mm [THT]"]
  LED6 = LED - 5mm [color="Red (633nm)" package="5 mm [THT]"]
  LED7 = LED - 5mm [color="Red (633nm)" package="5 mm [THT]"]
  LED8 = LED - 5mm [color="Red (633nm)" package="5 mm [THT]"]
  R1 = Resistor [tolerance=±5% resistance=220 package=THT]
  R2 = Resistor [tolerance=±5% resistance=220 package=THT]
  R3 = Resistor [tolerance=±5% resistance=220 package=THT]
  R4 = Resistor [tolerance=±5% resistance=220 package=THT]
  R5 = Resistor [tolerance=±5% resistance=220 package=THT]
  R6 = Resistor [tolerance=±5% resistance=220 package=THT]
  R7 = Resistor [tolerance=±5% resistance=220 package=THT]
  R8 = Resistor [tolerance=±5% resistance=220 package=THT]
  Part1 = Arduino Uno (Rev3)
  S1 = Pushbutton [package="[THT]"]
  R9 = Resistor [tolerance=±5% resistance=220 package=THT]

nets:
  N1: LED1.cathode, Part1.D0/RX
  N2: LED1.anode, R8.Pin_0
  N3: LED2.cathode, Part1.D5_PWM
  N4: LED2.anode, R3.Pin_0
  N5: LED3.cathode, Part1.D4
  N6: LED3.anode, R4.Pin_0
  N7: LED4.cathode, Part1.D3_PWM
  N8: LED4.anode, R5.Pin_0
  N9: LED5.cathode, Part1.D2
  N10: LED5.anode, R6.Pin_0
  N11: LED6.cathode, Part1.D1/TX
  N12: LED6.anode, R7.Pin_0
  N13: LED7.cathode, Part1.D6_PWM
  N14: LED7.anode, R2.Pin_0
  N15: LED8.cathode, Part1.D7
  N16: LED8.anode, R1.Pin_0
  N17: R1.Pin_1, R2.Pin_1, R3.Pin_1, R4.Pin_1, R6.Pin_1, R7.Pin_1, R8.Pin_1, Part1.GND, S1.Pin_1, S1.Pin_2
  N18: Part1.A0, S1.Pin_3, S1.Pin_4, R9.Pin_0
