# Fritzing sketch Untitled Sketch2 (saved by Fritzing 0.9.4)
breadboards: 1

parts:
  Part1 = Arduino Uno (Rev3)
  R1 = Resistor [tolerance=±5% resistance=220 package=THT]
  LED1 = LED - 5mm [color="Red (633nm)" package="5 mm [THT]"]
  R2 = Resistor [tolerance=±5% resistance=220 package=THT]
  LED2 = LED - 5mm [color="Red (633nm)" package="5 mm [THT]"]

nets:
  N1: Part1.D9_PWM, LED1.cathode
  N2: Part1.D13/SCK, LED2.cathode
  N3: Part1.GND, R1.Pin_1, R2.Pin_1
  N4: R1.Pin_0, LED1.anode
  N5: R2.Pin_0, LED2.anode
