# Fritzing sketch Untitled Sketch3-1 (saved by Fritzing 0.9.4)
breadboards: 1

parts:
  S1 = Pushbutton [package="[THT]"]
  Part1 = Arduino Uno (Rev3)
  R1 = Resistor [tolerance=±5% resistance=220 package=THT]
  LED1 = LED - 5mm [color="Red (633nm)" package="5 mm [THT]"]
  R2 = Resistor [tolerance=±5% resistance=220 package=THT]

nets:
  N1: S1.Pin_1, S1.Pin_2, Part1.D8, R1.Pin_0
  N2: S1.Pin_3, S1.Pin_4, Part1.GND, R2.Pin_1
  N3: Part1.D2, LED1.cathode
  N4: Part1.5V, R1.Pin_1
  N5: LED1.anode, R2.Pin_0
