# Fritzing sketch fritzing2 (saved by Fritzing 0.9.4)
breadboards: 1

parts:
  R1 = Resistor [tolerance=±5% resistance=220 package=THT]
  LED1 = LED - 5mm [color="Red (633nm)" package="5 mm [THT]"]
  S1 = Pushbutton [package="[SMD]"]
  Part3 = Arduino Uno (Rev3)
  R2 = Resistor [tolerance=±5% resistance=220 package=THT]

nets:
  N1: R1.Pin_0, Part3.GND, R2.Pin_1
  N2: R1.Pin_1, LED1.cathode
  N3: LED1.anode, Part3.D2
  N4: S1.Pin_1, S1.Pin_2, Part3.D8, R2.Pin_0
  N5: S1.Pin_3, S1.Pin_4, Part3.5V
