# Fritzing sketch fritzing3 (saved by Fritzing 0.9.4)
breadboards: 1

parts:
  LED1 = LED - 5mm [color="Red (633nm)" package="5 mm [THT]"]
  LED2 = LED - 5mm [color="Red (633nm)" package="5 mm [THT]"]
  LED3 = LED - 5mm [color="Red (633nm)" package="5 mm [THT]"]
  LED4 = LED - 5mm [color="Red (633nm)" package="5 mm [THT]"]
  R1 = Resistor [tolerance=±5% resistance=220 package=THT]
  R2 = Resistor [tolerance=±5% resistance=220 package=THT]
  R3 = Resistor [tolerance=±5% resistance=220 package=THT]
  R4 = Resistor [tolerance=±5% resistance=220 package=THT]
  Part1 = Arduino Uno (Rev3)
  R5 = Resistor [tolerance=±5% resistance=220 package=THT]
  S1 = Pushbutton [package="[THT]"]

nets:
  N1: LED1.cathode, Part1.D3_PWM
  N2: LED1.anode, R1.Pin_0
  N3: LED2.cathode, Part1.D2
  N4: LED2.anode, R2.Pin_0
  N5: LED3.cathode, Part1.D1/TX
  N6: LED3.anode, R3.Pin_0
  N7: LED4.cathode, Part1.D0/RX
  N8: LED4.anode, R4.Pin_0
  N9: R1.Pin_1, R2.Pin_1, R3.Pin_1, R4.Pin_1, S1.Pin_1, S1.Pin_2
  N10: Part1.A0, R5.Pin_0, S1.Pin_3, S1.Pin_4
  N11: Part1.GND, R5.Pin_1
